// Logisim project 4bitAdder.circ as structural Verilog: 9 circuits, main circuit main
// Number Correct
module main (
  input  Enable_Halt
);

  wire and_2_out, CLK, Correct, Halt, not_1_out, not_2_out, NotDone, YourCout;
  wire [3:0] A, B, YourSum;
  wire [4:0] Solution;
  wire [8:0] Number_Correct_q;

  not not_1 (not_1_out, Correct);
  and and_1 (Halt, Enable_Halt, not_1_out);
  Clock clock_1 (.out(CLK));
  Inputs inputs_1 (.Halt(Halt), .Clk(CLK), .A(A), .B(B), .NotDone(NotDone));
  // Probe on A
  // Probe on B
  // Probe on YourSum
  // Probe on YourCout
  // Probe on Solution[3:0]
  // Probe on Solution[4]
  _4bitAdder _4BitAdder (.A(A), .B(B), .Cin(1'b0), .Sum(YourSum), .Cout(YourCout));
  not not_2 (not_2_out, Halt);
  and and_2 (and_2_out, Correct, NotDone, not_2_out);
  Checker checker_1 (.A(A), .B(B), .Sum(YourSum), .Cout(YourCout), .Correct(Correct), .CorrectAnswer(Solution));
  Counter #(.width(9), .max('h100)) Number_Correct (
    .count(and_2_out), .Q(Number_Correct_q), .clk(CLK));  // open: load, D, carry, clr
  // Probe on Number_Correct_q

  // Notes on the sheet:
  //   Use the Poke Tool on the enable halt input to enable/disable halting
  //   Enabling Halt will cause the testing to stop as soon as the first incorrect answer is detected
endmodule

module _4bitAdder (
  input  [3:0] A,
  input  [3:0] B,
  input  Cin,
  output [3:0] Sum,
  output Cout
);

  wire c1_1_c1, c2_1_c2, c3_1_c3;

  C1 c1_1 (.cin(Cin), .A0(A[0]), .B0(B[0]), .C1(c1_1_c1));
  C2 c2_1 (.cin(Cin), .A0(A[0]), .B0(B[0]), .A1(A[1]), .B1(B[1]), .C2(c2_1_c2));
  C3 c3_1 (.cin(Cin), .A1(A[0]), .B0(B[0]), .A1_2(A[1]), .B1(B[1]), .A2(A[2]), .B2(B[2]), .C3(c3_1_c3));
  C4 c4_1 (
    .cin(Cin), .A1(A[0]), .B0(B[0]), .A1_2(A[1]), .B1(B[1]), .A2(A[2]), .A2_2(B[2]), .A3(A[3]), .B3(B[3]),
    .C4(Cout));
  full_adder full_adder_1 (.A(A[0]), .B(B[0]), .cin(Cin), .sum(Sum[0]));  // open: cout
  full_adder full_adder_2 (.A(A[1]), .B(B[1]), .cin(c1_1_c1), .sum(Sum[1]));  // open: cout
  full_adder full_adder_3 (.A(A[2]), .B(B[2]), .cin(c2_1_c2), .sum(Sum[2]));  // open: cout
  full_adder full_adder_4 (.A(A[3]), .B(B[3]), .cin(c3_1_c3), .sum(Sum[3]));  // open: cout
endmodule

module Inputs (
  input  Halt,
  input  Clk,
  output [3:0] A,
  output [3:0] B,
  output NotDone
);

  wire A_carry, and_1_out, and_2_out, and_3_out, and_4_out, CarryB, Delay_q, nHalt;

  not not_1 (nHalt, Halt);
  and and_1 (and_1_out, nHalt, NotDone);
  Counter #(.width(4), .max('hf)) u_B (.count(and_1_out), .Q(B), .carry(CarryB), .clk(Clk));  // open: load, D, clr
  and and_2 (and_2_out, nHalt, CarryB);
  Counter #(.width(4), .max('hf), .ongoal("stay")) u_A (
    .count(and_2_out), .Q(A), .carry(A_carry), .clk(Clk));  // open: load, D, clr
  and and_3 (and_3_out, CarryB, A_carry);
  Register #(.width(1)) Delay (.D(and_3_out), .en(and_4_out), .Q(Delay_q), .clk(Clk));  // open: clr
  and and_4 (and_4_out, nHalt, NotDone);
  not not_2 (NotDone, Delay_q);
endmodule

module Checker (
  input  [3:0] A,
  input  [3:0] B,
  input  [3:0] Sum,
  input  Cout,
  output Correct,
  output [4:0] CorrectAnswer
);

  ROM #(.dataWidth(5)) rom_1 (.addr({A, B}), .data(CorrectAnswer));  // open: sel
  Comparator #(.width(5), .mode("unsigned")) comparator_1 (
    .a(CorrectAnswer), .b({Cout, Sum}), .eq(Correct));  // open: gt, lt

  // Other names for the same wires on the sheet: StudentSol[4:0] = {Cout, Sum}

  // Notes on the sheet:
  //   contents of rom_1 (hex, n*v repeats v):
  //   0 1 2 3 4 5 6 7 8 9 a b c d e f 1 2 3 4 5 6 7 8 9 a b c d e f 10 2 3 4 5 6 7 8 9 a b c d e f 10 11 3
  //   4 5 6 7 8 9 a b c d e f 10 11 12 4 5 6 7 8 9 a b c d e f 10 11 12 13 5 6 7 8 9 a b c d e f 10 11 12
  //   13 14 6 7 8 9 a b c d e f 10 11 12 13 14 15 7 8 9 a b c d e f 10 11 12 13 14 15 16 8 9 a b c d e f
  //   10 11 12 13 14 15 16 17 9 a b c d e f 10 11 12 13 14 15 16 17 18 a b c d e f 10 11 12 13 14 15 16 17
  //   18 19 b c d e f 10 11 12 13 14 15 16 17 18 19 1a c d e f 10 11 12 13 14 15 16 17 18 19 1a 1b d e f
  //   10 11 12 13 14 15 16 17 18 19 1a 1b 1c e f 10 11 12 13 14 15 16 17 18 19 1a 1b 1c 1d f 10 11 12 13
  //   14 15 16 17 18 19 1a 1b 1c 1d 1e
endmodule

module full_adder (
  input  A,
  input  B,
  input  cin,
  output sum,
  output cout
);

  wire and_1_out, xor_1_out;

  xor xor_1 (xor_1_out, A, B);
  and and_1 (and_1_out, A, B);
  // AND_Gate and_2 has open pins: in1=xor_1_out, out=open
  or or_1 (cout, cin, and_1_out);
  xor xor_2 (sum, xor_1_out, cin);
endmodule

module C1 (
  input  cin,
  input  A0,
  input  B0,
  output C1
);

  wire and_1_out, and_2_out, xor_1_out;

  and and_1 (and_1_out, cin, xor_1_out);
  xor xor_1 (xor_1_out, A0, B0);
  and and_2 (and_2_out, A0, B0);
  or or_1 (C1, and_1_out, and_2_out);
endmodule

module C2 (
  input  cin,
  input  A0,
  input  B0,
  input  A1,
  input  B1,
  output C2
);

  wire and_1_out, and_2_out, c1_1_c1, xor_1_out;

  C1 c1_1 (.cin(cin), .A0(A0), .B0(B0), .C1(c1_1_c1));
  and and_1 (and_1_out, c1_1_c1, xor_1_out);
  xor xor_1 (xor_1_out, A1, B1);
  and and_2 (and_2_out, A1, B1);
  or or_1 (C2, and_1_out, and_2_out);
endmodule

module C3 (
  input  cin,
  input  A1,
  input  B0,
  input  A1_2,
  input  B1,
  input  A2,
  input  B2,
  output C3
);

  wire and_1_out, and_2_out, c2_1_c2, xor_1_out;

  C2 c2_1 (.cin(cin), .A0(A1), .B0(B0), .A1(A1_2), .B1(B1), .C2(c2_1_c2));
  xor xor_1 (xor_1_out, A2, B2);
  and and_1 (and_1_out, c2_1_c2, xor_1_out);
  and and_2 (and_2_out, A2, B2);
  or or_1 (C3, and_1_out, and_2_out);
endmodule

module C4 (
  input  cin,
  input  A1,
  input  B0,
  input  A1_2,
  input  B1,
  input  A2,
  input  A2_2,
  input  A3,
  input  B3,
  output C4
);

  wire and_1_out, and_2_out, c3_1_c3, xor_1_out;

  C3 c3_1 (.cin(cin), .A1(A1), .B0(B0), .A1_2(A1_2), .B1(B1), .A2(A2), .B2(A2_2), .C3(c3_1_c3));
  xor xor_1 (xor_1_out, A3, B3);
  and and_1 (and_1_out, c3_1_c3, xor_1_out);
  and and_2 (and_2_out, A3, B3);
  or or_1 (C4, and_1_out, and_2_out);
endmodule
