// Logisim project Vending.circ as structural Verilog: 12 circuits, main circuit main
module main (
  input  Halt_Enable
);

  wire and_2_out, CLK, Correct, Dime, Done_Testing, Give_Dime, Give_Merch, Give_Nickel, Halt, Nickel,
       not_1_out, not_2_out, not_3_out, Quarter, Sol_Give_Dime, Sol_Give_Merch, Sol_Give_Nickel;
  wire [8:0] counter_1_q, TestNumber;

  Clock clock_1 (.out(CLK));
  not not_1 (not_1_out, Correct);
  and and_1 (Halt, Halt_Enable, not_1_out);
  Inputs inputs_1 (
    .Halt(Halt), .CLK(CLK), .Quarter(Quarter), .Dime(Dime), .Nickel(Nickel), .TestNumber(TestNumber),
    .Done_Testing(Done_Testing));
  // Probe on Quarter
  // Probe on Dime
  // Probe on Nickel
  Vending vending_1 (
    .Quarter(Quarter), .Dime(Dime), .Nickel(Nickel), .CLK(CLK), .Give_Merchandise(Give_Merch),
    .Give_Dime(Give_Dime), .Give_Nickel(Give_Nickel));
  // Probe on Correct
  // Probe on Give_Merch
  // Probe on Sol_Give_Merch
  // Probe on Give_Dime
  // Probe on Sol_Give_Dime
  // Probe on Give_Nickel
  // Probe on Sol_Give_Nickel
  not not_2 (not_2_out, Halt);
  Checker checker_1 (
    .Give_Merch(Give_Merch), .Give_Dime(Give_Dime), .Give_Nickel(Give_Nickel), .TestNumber(TestNumber),
    .Correct(Correct), .Sol_Give_Merch(Sol_Give_Merch), .Sol_Give_Dime(Sol_Give_Dime),
    .Sol_Give_Nickel(Sol_Give_Nickel));
  and and_2 (and_2_out, Correct, not_2_out, not_3_out);
  not not_3 (not_3_out, Done_Testing);
  // Probe on counter_1_q
  Counter #(.width(9), .max('h162), .ongoal("stay")) counter_1 (
    .count(and_2_out), .Q(counter_1_q), .clk(CLK));  // open: load, D, carry, clr

  // Notes on the sheet:
  //   Max 354
endmodule

module Vending (
  input  Quarter,
  input  Dime,
  input  Nickel,
  input  CLK,
  output Give_Merchandise,
  output Give_Dime,
  output Give_Nickel
);

  wire d1_1_g, d2_1_g, d3_1_g, d_ff_1_q, d_ff_2_q, d_ff_3_q;

  D1 d1_1 (.a(d_ff_1_q), .b(d_ff_2_q), .c(d_ff_3_q), .d(Quarter), .e(Dime), .f(Nickel), .g(d1_1_g));
  D2 d2_1 (.a(d_ff_1_q), .b(d_ff_2_q), .c(d_ff_3_q), .d(Quarter), .e(Dime), .f(Nickel), .g(d2_1_g));
  D3 d3_1 (.a(d_ff_1_q), .b(d_ff_2_q), .c(d_ff_3_q), .d(Quarter), .e(Dime), .f(Nickel), .g(d3_1_g));
  D_Flip_Flop d_ff_1 (.clk(CLK), .D(d1_1_g), .Q(d_ff_1_q));  // open: Qn, preset, en, reset
  D_Flip_Flop d_ff_2 (.clk(CLK), .D(d2_1_g), .Q(d_ff_2_q));  // open: Qn, preset, en, reset
  D_Flip_Flop d_ff_3 (.clk(CLK), .D(d3_1_g), .Q(d_ff_3_q));  // open: Qn, preset, en, reset
  \output  output_1 (.a(d_ff_1_q), .b(d_ff_2_q), .c(d_ff_3_q), .d(Quarter), .e(Dime), .f(Nickel), .g(Give_Merchandise));
  D_Out d_out_1 (.a(d_ff_1_q), .b(d_ff_2_q), .c(d_ff_3_q), .d(Quarter), .e(Dime), .f(Nickel), .g(Give_Dime));
  N_Out n_out_1 (.a(d_ff_1_q), .b(d_ff_2_q), .c(d_ff_3_q), .d(Quarter), .e(Dime), .f(Nickel), .g(Give_Nickel));

  // Other names for the same wires on the sheet: Quater = Quarter
endmodule

module Inputs (
  input  Halt,
  input  CLK,
  output Quarter,
  output Dime,
  output Nickel,
  output [8:0] TestNumber,
  output Done_Testing
);

  wire not_1_out;

  not not_1 (not_1_out, Halt);
  Counter #(.width(9), .max('h162), .ongoal("stay")) counter_1 (
    .count(not_1_out), .Q(TestNumber), .carry(Done_Testing), .clk(CLK));  // open: load, D, clr
  ROM #(.addrWidth(9), .dataWidth(3)) rom_1 (.addr(TestNumber), .data({Quarter, Dime, Nickel}));  // open: sel

  // Notes on the sheet:
  //   contents of rom_1 (hex, n*v repeats v):
  //   1 0 1 0 1 0 1 0 1 0 1 0 1 0 1 0 1 0 1 0 1 0 2 0 1 0 1 0 1 0 1 0 1 0 4 0 1 0 1 0 1 0 1 0 2 0 1 0 1 0
  //   1 0 1 0 4 0 1 0 1 0 1 0 1 0 2 0 1 0 1 0 1 0 2 0 2 0 1 0 1 0 1 0 2 0 4 0 1 0 1 0 1 0 4 0 1 0 1 0 1 0
  //   1 0 2 0 1 0 1 0 1 0 2 0 2 0 1 0 1 0 1 0 2 0 4 0 1 0 1 0 2 0 2 0 1 0 1 0 2 0 4 0 1 0 1 0 4 0 1 0 1 0
  //   1 0 1 0 2 0 1 0 1 0 1 0 2 0 2 0 1 0 1 0 1 0 2 0 4 0 1 0 1 0 2 0 2 0 1 0 1 0 2 0 4 0 1 0 1 0 2 0 2 0
  //   1 0 2 0 2 0 2 0 1 0 2 0 2 0 4 0 1 0 2 0 4 0 1 0 4 0 1 0 1 0 1 0 1 0 2 0 1 0 1 0 1 0 2 0 2 0 1 0 1 0
  //   1 0 2 0 4 0 1 0 1 0 2 0 2 0 1 0 1 0 2 0 4 0 1 0 1 0 2 0 2 0 1 0 2 0 2 0 2 0 1 0 2 0 2 0 4 0 1 0 2 0
  //   4 0 1 0 1 0 2 0 2 0 1 0 2 0 2 0 2 0 1 0 2 0 2 0 4 0 2 0 2 0 2 0 2 0 2 0 4 0 2 0 4 0 1 0 4 0 2 0 4 0
  //   4 0 4
endmodule

module Checker (
  input  Give_Merch,
  input  Give_Dime,
  input  Give_Nickel,
  input  [8:0] TestNumber,
  output Correct,
  output Sol_Give_Merch,
  output Sol_Give_Dime,
  output Sol_Give_Nickel
);

  ROM #(.addrWidth(9), .dataWidth(3)) rom_1 (
    .addr(TestNumber), .data({Sol_Give_Merch, Sol_Give_Dime, Sol_Give_Nickel}));  // open: sel
  Comparator #(.width(3)) comparator_1 (
    .a({Sol_Give_Merch, Sol_Give_Dime, Sol_Give_Nickel}), .b({Give_Merch, Give_Dime, Give_Nickel}),
    .eq(Correct));  // open: gt, lt

  // Other names for the same wires on the sheet: Solution[2:0] = {Sol_Give_Merch, Sol_Give_Dime, Sol_Give_Nickel};
  //   Your_Answer[2:0] = {Give_Merch, Give_Dime, Give_Nickel}

  // Notes on the sheet:
  //   contents of rom_1 (hex, n*v repeats v):
  //   10*0 4 11*0 5 11*0 7 9*0 4 9*0 7 9*0 4 9*0 5 9*0 7 7*0 6 9*0 4 9*0 5 9*0 7 7*0 4 7*0 7 5*0 5 9*0 4
  //   9*0 5 9*0 7 7*0 4 7*0 7 7*0 4 7*0 5 7*0 7 5*0 6 0 0 0 4 9*0 4 9*0 5 9*0 7 7*0 4 7*0 7 7*0 4 7*0 5
  //   7*0 7 5*0 6 7*0 4 7*0 5 7*0 7 5*0 4 5*0 7 0 0 0 5 0 0 0 4 0 0 0 5 0 0 0 7
endmodule

module D1 (
  input  a,
  input  b,
  input  c,
  input  d,
  input  e,
  input  f,
  output g
);

  wire and_1_out, and_2_out, and_3_out, and_4_out, and_5_out, not_1_out, not_2_out, not_3_out, not_4_out,
       not_5_out, not_6_out, not_7_out, not_8_out;

  not not_1 (not_1_out, a);
  not not_2 (not_2_out, b);
  not not_3 (not_3_out, c);
  not not_4 (not_4_out, d);
  not not_5 (not_5_out, e);
  not not_6 (not_6_out, d);
  not not_7 (not_7_out, e);
  not not_8 (not_8_out, f);
  and and_1 (and_1_out, not_1_out, not_2_out, d);
  and and_2 (and_2_out, b, e);
  and and_3 (and_3_out, b, c, f);
  and and_4 (and_4_out, a, not_3_out, not_4_out, not_5_out);
  and and_5 (and_5_out, a, not_6_out, not_7_out, not_8_out);
  or or_1 (g, and_1_out, and_2_out, and_3_out, and_4_out, and_5_out);
endmodule

module D2 (
  input  a,
  input  b,
  input  c,
  input  d,
  input  e,
  input  f,
  output g
);

  wire and_1_out, and_2_out, and_3_out, and_4_out, not_1_out, not_2_out, not_3_out, not_4_out, not_5_out,
       not_6_out, not_7_out, not_8_out;

  not not_1 (not_1_out, a);
  not not_2 (not_2_out, b);
  not not_3 (not_3_out, a);
  not not_4 (not_4_out, b);
  not not_5 (not_5_out, d);
  not not_6 (not_6_out, e);
  not not_7 (not_7_out, f);
  not not_8 (not_8_out, c);
  and and_1 (and_1_out, not_1_out, not_2_out, e);
  and and_2 (and_2_out, not_3_out, not_4_out, c, f);
  and and_3 (and_3_out, b, not_5_out, not_6_out, not_7_out);
  and and_4 (and_4_out, b, not_8_out, f);
  or or_1 (g, and_1_out, and_2_out, and_3_out, and_4_out);
endmodule

module D3 (
  input  a,
  input  b,
  input  c,
  input  d,
  input  e,
  input  f,
  output g
);

  wire and_1_out, and_2_out, and_3_out, and_4_out, not_1_out, not_2_out, not_3_out, not_4_out, not_5_out,
       not_6_out, not_7_out, not_8_out;

  not not_1 (not_1_out, c);
  not not_2 (not_2_out, a);
  not not_3 (not_3_out, b);
  not not_4 (not_4_out, c);
  not not_5 (not_5_out, d);
  not not_6 (not_6_out, e);
  not not_7 (not_7_out, f);
  not not_8 (not_8_out, a);
  and and_1 (and_1_out, not_1_out, f);
  and and_2 (and_2_out, not_2_out, not_3_out, not_4_out, d);
  and and_3 (and_3_out, c, not_5_out, not_6_out, not_7_out);
  and and_4 (and_4_out, not_8_out, c, e);
  or or_1 (g, and_1_out, and_2_out, and_3_out, and_4_out);
endmodule

module \output  (
  input  a,
  input  b,
  input  c,
  input  d,
  input  e,
  input  f,
  output g
);

  wire and_1_out, and_2_out, and_3_out, and_4_out, and_5_out;

  and and_1 (and_1_out, c, d);
  and and_2 (and_2_out, b, d);
  and and_3 (and_3_out, a, e);
  and and_4 (and_4_out, a, d);
  and and_5 (and_5_out, a, c, f);
  or or_1 (g, and_1_out, and_2_out, and_3_out, and_4_out, and_5_out);
endmodule

module D_Out (
  input  a,
  input  b,
  input  c,
  input  d,
  input  e,
  input  f,
  output g
);

  wire and_1_out, and_2_out;

  and and_1 (and_1_out, b, c, d);
  and and_2 (and_2_out, a, d);
  or or_1 (g, and_1_out, and_2_out);
endmodule

module N_Out (
  input  a,
  input  b,
  input  c,
  input  d,
  input  e,
  input  f,
  output g
);

  wire and_1_out, and_2_out, and_3_out, not_1_out;

  not not_1 (not_1_out, c);
  and and_1 (and_1_out, b, not_1_out, d);
  and and_2 (and_2_out, a, d);
  and and_3 (and_3_out, a, c, e);
  or or_1 (g, and_1_out, and_2_out, and_3_out);
endmodule

module backup (
  input  Quarter,
  input  Dime,
  input  Nickel,
  input  CLK,
  output Give_Merchandise,
  output Give_Dime,
  output Give_Nickel
);

  wire d1_1_g, d2_1_g, d3_1_g, d_ff_1_q, d_ff_2_q, d_ff_3_q;

  D1 d1_1 (.a(d_ff_1_q), .b(d_ff_2_q), .c(d_ff_3_q), .d(Quarter), .e(Dime), .f(Nickel), .g(d1_1_g));
  D2 d2_1 (.a(d_ff_1_q), .b(d_ff_2_q), .c(d_ff_3_q), .d(Quarter), .e(Dime), .f(Nickel), .g(d2_1_g));
  D3 d3_1 (.a(d_ff_1_q), .b(d_ff_2_q), .c(d_ff_3_q), .d(Quarter), .e(Dime), .f(Nickel), .g(d3_1_g));
  D_Flip_Flop d_ff_1 (.clk(CLK), .D(d1_1_g), .Q(d_ff_1_q));  // open: Qn, preset, en, reset
  D_Flip_Flop d_ff_2 (.clk(CLK), .D(d2_1_g), .Q(d_ff_2_q));  // open: Qn, preset, en, reset
  D_Flip_Flop d_ff_3 (.clk(CLK), .D(d3_1_g), .Q(d_ff_3_q));  // open: Qn, preset, en, reset
  \output  output_1 (.a(d_ff_1_q), .b(d_ff_2_q), .c(d_ff_3_q), .d(Quarter), .e(Dime), .f(Nickel), .g(Give_Merchandise));
  D_Out d_out_1 (.a(d_ff_1_q), .b(d_ff_2_q), .c(d_ff_3_q), .d(Quarter), .e(Dime), .f(Nickel), .g(Give_Dime));
  D_Out d_out_2 (.a(d_ff_1_q), .b(d_ff_2_q), .c(d_ff_3_q), .d(Quarter), .e(Dime), .f(Nickel), .g(Give_Nickel));

  // Other names for the same wires on the sheet: Quater = Quarter
endmodule

module back_2 (
  input  Quarter,
  input  Dime,
  input  Nickel,
  input  CLK,
  output Give_Merchandise,
  output Give_Dime,
  output Give_Nickel
);

  wire d1_1_g, d2_1_g, d3_1_g, d_ff_1_q, d_ff_1_qn, d_ff_2_q, d_ff_2_qn, d_ff_3_q, d_ff_3_qn;

  D1 d1_1 (.a(d_ff_1_qn), .b(d_ff_2_qn), .c(d_ff_3_qn), .d(Quarter), .e(Dime), .f(Nickel), .g(d1_1_g));
  D2 d2_1 (.a(d_ff_1_qn), .b(d_ff_2_qn), .c(d_ff_3_qn), .d(Quarter), .e(Dime), .f(Nickel), .g(d2_1_g));
  D3 d3_1 (.a(d_ff_1_qn), .b(d_ff_2_qn), .c(d_ff_3_qn), .d(Quarter), .e(Dime), .f(Nickel), .g(d3_1_g));
  D_Flip_Flop d_ff_1 (.clk(CLK), .D(d1_1_g), .Q(d_ff_1_q), .Qn(d_ff_1_qn));  // open: preset, en, reset
  D_Flip_Flop d_ff_2 (.clk(CLK), .D(d2_1_g), .Q(d_ff_2_q), .Qn(d_ff_2_qn));  // open: preset, en, reset
  D_Flip_Flop d_ff_3 (.clk(CLK), .D(d3_1_g), .Q(d_ff_3_q), .Qn(d_ff_3_qn));  // open: preset, en, reset
  \output  output_1 (.a(d_ff_1_q), .b(d_ff_2_q), .c(d_ff_3_q), .d(Quarter), .e(Dime), .f(Nickel), .g(Give_Merchandise));
  D_Out d_out_1 (.a(d_ff_1_q), .b(d_ff_2_q), .c(d_ff_3_q), .d(Quarter), .e(Dime), .f(Nickel), .g(Give_Dime));
  D_Out d_out_2 (.a(d_ff_1_q), .b(d_ff_2_q), .c(d_ff_3_q), .d(Quarter), .e(Dime), .f(Nickel), .g(Give_Nickel));

  // Other names for the same wires on the sheet: Quater = Quarter
endmodule
